# Fritzing sketch Experience 1 (saved by Fritzing 0.9.3b)
breadboards: 1

parts:
  Arduino_UNO = Arduino Uno (Rev3)
  MAIN = Ceramic Capacitor [capacitance=10nF package="100 mil [THT, multilayer]"]
  L1 = Inductor [package="400 mil [THT]"]
  R1 = Resistor [tolerance=±5% resistance=560 package=THT]
  R2 = Resistor [tolerance=±5% resistance=1M package=THT]

nets (from the schematic view):
  N1: Arduino_UNO.A0, MAIN.0, L1.pin_0, R2.Pin_1
  N2: Arduino_UNO.D9_PWM, R1.Pin_1
  N3: Arduino_UNO.GND, R2.Pin_0
  N4: L1.pin_1, R1.Pin_0
