# Fritzing sketch Experience 2 (saved by Fritzing 0.9.3b)
breadboards: 1

parts:
  Arduino_UNO = Arduino Uno (Rev3)
  C1 = Ceramic Capacitor [capacitance=0.1nF package="100 mil [THT, multilayer]"]
  R2 = Resistor [tolerance=±5% resistance=1M package=THT]
  D1 = Rectifier Diode [part_number=1N64548 package="300 mil [THT]"]
  L1 = Inductor [inductance=10mH package="400 mil [THT]"]
  R1 = Resistor [tolerance=±5% resistance=10k package=THT]
  R3 = Resistor [tolerance=±5% resistance=3.3k package=THT]
  C2 = Ceramic Capacitor [capacitance=100nF package="100 mil [THT, multilayer]"]

nets (from the schematic view):
  N1: Arduino_UNO.A0, C1.1, R2.Pin_0, D1.cathode
  N2: Arduino_UNO.D9_PWM, R1.Pin_1
  N3: Arduino_UNO.GND, C1.0, R2.Pin_1, R3.Pin_1
  N4: D1.anode, L1.pin_0, C2.0
  N5: L1.pin_1, R1.Pin_0, R3.Pin_0
