# Fritzing sketch Potatoe404 (saved by Fritzing 0.9.3b)
breadboards: 1

parts:
  Composant1 = Arduino Uno (Rev3)
  C1 = Ceramic Capacitor [capacitance=0.1nF package="100 mil [THT, multilayer]"]
  R2 = Resistor [tolerance=±5% resistance=1M package=THT]
  D1 = Rectifier Diode [part_number=1N64548 package="300 mil [THT]"]
  L1 = Inductor [inductance=10mH package="400 mil [THT]"]
  R1 = Resistor [tolerance=±5% resistance=10k package=THT]
  R3 = Resistor [tolerance=±5% resistance=3.3k package=THT]
  C2 = Ceramic Capacitor [capacitance=100nF package="100 mil [THT, multilayer]"]
  LED1 = LED - 5mm [color="Red (633nm)" package="5 mm [THT]"]
  LED2 = LED - 5mm [color="Green (560nm)" package="5 mm [THT]"]
  LED3 = LED - 5mm [color="Yellow (585nm)" package="5 mm [THT]"]
  BUZZEUR = Piezo Speaker

nets (from the schematic view):
  N1: Composant1.A0, C1.1, R2.Pin_0, D1.cathode
  N2: Composant1.D9_PWM, R1.Pin_1
  N3: Composant1.D10_PWM/SS, BUZZEUR.pin1
  N4: Composant1.D3_PWM, LED1.anode
  N5: Composant1.D5_PWM, LED2.anode
  N6: Composant1.D6_PWM, LED3.anode
  N7: Composant1.GND, C1.0, R2.Pin_1, R3.Pin_1, LED1.cathode, LED2.cathode, LED3.cathode, BUZZEUR.pin2
  N8: D1.anode, L1.pin_0, C2.0
  N9: L1.pin_1, R1.Pin_0, R3.Pin_0
